# Fritzing sketch Adafruit.Ultimate.GPS.RPiZero (saved by Fritzing 0.9.3b)

parts:
  Part1 = Adafruit Ultimate GPS v3 [part_number="Adafruit #746"]
  Raspberry_Pi_Zero1 = Raspberry Pi Zero

nets:
  VIN: Part1.VIN, Raspberry_Pi_Zero1.5V
  GND: Part1.GND, Raspberry_Pi_Zero1.GND
  N1: Part1.RX, Raspberry_Pi_Zero1.GPIO14
  N2: Part1.TX, Raspberry_Pi_Zero1.GPIO15

custom parts:
  Adafruit Ultimate GPS v3: We carry a few different GPS modules here in the Adafruit shop, but none that satisfied our every desire - that's why we designed this little GPS breakout board. We believe this is the Ultimate GPS module, so we named it that. It's got everything you want and more: -165 dBm sensitivity, 10 Hz updates, 66 channels 5V friendly design and only 20mA current draw Breadboard friendly + two mounting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
