# Fritzing sketch relay (saved by Fritzing 0.9.4)

parts:
  Relay_5V2 = Keyes Relay [package=THT]
  Raspberry_Pi_1 = Raspberry Pi 3 [part_number=RPI-3-V1.2]

nets:
  N1: Relay_5V2.signal, Raspberry_Pi_1.GIPO17
  N2: Relay_5V2.power, Raspberry_Pi_1.3v3
  N3: Relay_5V2.ground, Raspberry_Pi_1.GND

notes:
  NO - Naturally Open
  C - COM
  Relay ON: NO & COM are connected
  Blue: Pin #11, BCM 17, GPIO_0
  Black: GND
  Red: 3V3

custom parts:
  Keyes Relay: The Keyes 5V relay module is suitable for SCM development, home appliance control. It uses a 5V~12V TIL control signal which can control DC / AC signal.
